# Fritzing sketch breaboard (saved by Fritzing 0.9.2b)
circuit board: 8.46667cm x 5.64444cm
breadboards: 5

parts:
  VCC1 = Battery
  VCC2 = Battery
  Q1 = NPN-Transistor [package="TO92 [THT]"]
  M1 = DC Motor
  M2 = DC Motor
  MBED1 = mbed
  Q2 = NPN-Transistor [part_number=2N2222 package="TO92 [THT]"]
  Part1 = BH1750FVI Breakout Board [part_number=BH1750FVI]
  Part2 = BH1750FVI Breakout Board [part_number=BH1750FVI]
  BAT1 = BC9VPC [package=bc9vpc]
  R1 = Resistor [tolerance=±5% resistance=1k package="0603 [SMD]"]
  R2 = Resistor [tolerance=±5% resistance=1k package="0402 [SMD]"]
  Part3 = HC-SR04 Ultrasonic Rangemeter
  U1 = SWITCH-SPST-2 [package=switch-spst-vertical]

nets (from the breadboard view):
  N1: VCC1.-, VCC2.+
  N2: VCC1.+, Q1.E, Q2.E
  GND: VCC2.-, M1.pin_2, M2.pin_1, MBED1.GND, Part1.GND, Part2.GND, Part3.GND, U1.O
  N3: Q1.B, R1.Pin_1
  N4: Q1.C, M1.pin_1
  N5: M2.pin_2, Q2.C
  N6: MBED1.Vin, BAT1.V+
  N7: MBED1.pin5, Part3.Echo
  N8: MBED1.pin6, Part3.Trig
  N9: MBED1.pin9, Part1.SDA, Part2.SDA
  N10: MBED1.pin10, Part1.SCL, Part2.SCL
  N11: MBED1.pin26, R2.Pin_0
  N12: MBED1.pin27, R1.Pin_0
  VCC: MBED1.VOUT, Part1.VCC, Part2.ADD, Part2.VCC, Part3.VCC
  N13: Q2.B, R2.Pin_1
  N14: BAT1.V-, U1.P

custom parts:
  BH1750FVI Breakout Board: The ROHM Semiconductor BH1750FVI is a digital ambient light sensor for the I2C bus interface. The BH750FVI is able to detect a wide range of light intensities (1-65535 lux). The spectral range is similar to that of the human eye.
